# Fritzing sketch Montage (1) Vue Schématique (saved by Fritzing 0.9.3b)
breadboards: 1

parts:
  R1 = Resistor [tolerance=±5% resistance=220 package="0603 [SMD]"]
  R2 = Resistor [tolerance=±5% resistance=220 package="0603 [SMD]"]
  Composant1 = Arduino Uno (Rev3)
  C2 = Tantalum Capacitor [capacitance="1 μF" package="C 6032 [SMD, tantalum]"]
  U2 = LM124-324 Quad Opamp [package="DIP (Dual Inline)"]
  C3 = Ceramic Capacitor [capacitance="100 nF" package="1206 [SMD, multilayer]"]
  C4 = Ceramic Capacitor [capacitance="100 nF" package="1206 [SMD, multilayer]"]
  R3 = Resistor [tolerance=±5% resistance=220 package="0603 [SMD]"]
  R4 = Resistor [tolerance=±5% resistance=220 package="0603 [SMD]"]
  C5 = Tantalum Capacitor [capacitance=1μF package="100 mil [THT, tantalum]"]
  R5 = Resistor [tolerance=±5% resistance=220 package="0603 [SMD]"]
  R6 = Resistor [tolerance=±5% resistance=220 package="0603 [SMD]"]
  R7 = Resistor [tolerance=±5% resistance=220 package="0603 [SMD]"]
  Q1 = NPN-Transistor [package="SOT-23 [SMD]"]
  D1 = LTE-302 [package=lte-302]
  Q2 = LTR-301 [package=ltr-301]

nets (from the schematic view):
  N1: R1.Pin_0, R2.Pin_1, Composant1.5V, U2.VCC+, Q1.1
  N2: R1.Pin_1, C2.+, D1.A
  N3: R2.Pin_0, Q2.C
  N4: Composant1.A0, Q1.2
  N5: Composant1.GND, U2.VCC-, R3.Pin_0, R4.Pin_0, R5.Pin_0, D1.C, Q2.E
  N6: C2.-, U2.1IN+, R3.Pin_1
  N7: U2.1OUT, C4.1, C5.+
  N8: U2.1IN-, C4.0, R4.Pin_1
  N9: U2.4IN+, C5.-, R5.Pin_1
  N10: U2.4IN-, C3.0, R7.Pin_1
  N11: U2.4OUT, C3.1, R6.Pin_0, R7.Pin_0
  N12: R6.Pin_1, Q1.0
