# Fritzing sketch Montage (2) Vue Schématique (saved by Fritzing 0.9.3b)
breadboards: 1

parts:
  LED1 = smd LED [color="Red (633nm)" package="0805 [SMD]"]
  LED2 = smd LED [color="Red (633nm)" package="0805 [SMD]"]
  LED3 = smd LED [color="Red (633nm)" package="0805 [SMD]"]
  LED4 = smd LED [color="Red (633nm)" package="0805 [SMD]"]
  LED5 = smd LED [color="Red (633nm)" package="0805 [SMD]"]
  LED6 = smd LED [color="Red (633nm)" package="0805 [SMD]"]
  LED8 = smd LED [color="Red (633nm)" package="0805 [SMD]"]
  LED9 = smd LED [color="Red (633nm)" package="0805 [SMD]"]
  LED10 = smd LED [color="Red (633nm)" package="0805 [SMD]"]
  Composant1 = Arduino Uno (Rev3)
  R7 = Resistor [tolerance=±5% resistance=220 package=THT]
  R8 = Resistor [tolerance=±5% resistance=220 package=THT]
  R9 = Resistor [tolerance=±5% resistance=220 package=THT]
  R10 = Resistor [tolerance=±5% resistance=220 package=THT]
  R11 = Resistor [tolerance=±5% resistance=220 package=THT]
  R12 = Resistor [tolerance=±5% resistance=220 package=THT]
  R13 = Resistor [tolerance=±5% resistance=220 package=THT]
  R14 = Resistor [tolerance=±5% resistance=220 package=THT]
  R15 = Resistor [tolerance=±5% resistance=220 package=THT]
  R16 = Resistor [tolerance=±5% resistance=220 package=THT]
  LED11 = smd LED [color="Red (633nm)" package="0805 [SMD]"]

nets (from the schematic view):
  N1: LED1.cathode, LED2.cathode, LED3.cathode, LED4.cathode, LED5.cathode, LED6.cathode, LED8.cathode, LED9.cathode, LED10.cathode, Composant1.GND, R7.Pin_1, R8.Pin_1, R9.Pin_1, R10.Pin_1, R11.Pin_1, R12.Pin_1, R13.Pin_1, R14.Pin_1, R15.Pin_1, R16.Pin_1, LED11.cathode
  N2: LED1.anode, Composant1.A2, R9.Pin_0
  N3: LED2.anode, Composant1.A5/SCL, R12.Pin_0
  N4: LED3.anode, Composant1.A3, R10.Pin_0
  N5: LED4.anode, Composant1.A0, R7.Pin_0
  N6: LED5.anode, Composant1.D4, R15.Pin_0
  N7: LED6.anode, R14.Pin_0
  N8: LED8.anode, Composant1.D2, R13.Pin_0
  N9: LED9.anode, Composant1.A1, R8.Pin_0
  N10: LED10.anode, Composant1.A4/SDA, R11.Pin_0
  N11: Composant1.D7, R16.Pin_0, LED11.anode
