# Fritzing sketch Montage (saved by Fritzing 0.9.3b)
breadboards: 1

parts:
  R1 = Resistor [tolerance=±5% resistance=220 package=THT]
  R2 = Resistor [tolerance=±5% resistance=220 package=THT]
  R3 = Resistor [tolerance=±5% resistance=220 package=THT]
  R4 = Resistor [tolerance=±5% resistance=220 package=THT]
  R5 = Resistor [tolerance=±5% resistance=220 package=THT]
  Composant1 = Arduino Uno (Rev3)
  C1 = Tantalum Capacitor [capacitance=1μF package="100 mil [THT, tantalum]"]
  C2 = Tantalum Capacitor [capacitance=1μF package="100 mil [THT, tantalum]"]
  Q1 = NPN-Transistor [package="TO92 [THT]"]
  C3 = Capacitor [package=cap-pth-5mm]  # not connected
  C4 = Capacitor [package=cap-pth-5mm]
  Q2 = LTR-301 [package=ltr-301]  # not connected
  LED1 = LEDs [package=led10mm]
  R6 = Resistor [tolerance=±5% resistance=220 package=THT]
  R7 = Resistor [tolerance=±5% resistance=220 package=THT]
  U2 = LM124-324 Quad Opamp [package="DIP (Dual Inline)"]
  R8 = Resistor [tolerance=±5% resistance=220 package=THT]

nets:
  N1: R1.Pin_0, C4.1, U2.1IN-
  N2: R1.Pin_1, R2.Pin_1
  N3: R2.Pin_0, C2.+, U2.1IN+
  N4: R3.Pin_0, C1.-, C4.2, U2.1OUT
  N5: R4.Pin_0, R5.Pin_0, Composant1.5V, Q1.E, R8.Pin_0
  N6: R4.Pin_1, R5.Pin_1
  N7: Composant1.A0, Q1.C
  N8: LED1.C, R8.Pin_1
  N9: R6.Pin_0, R7.Pin_0, U2.4OUT
  N10: R6.Pin_1, U2.4IN-
