# Fritzing sketch vue platine montage coeur  (saved by Fritzing 0.9.3b)
breadboards: 1

parts:
  R1 = Resistor [tolerance=±5% resistance=220 package=THT]
  LED1 = LED - 5mm [color="Red (633nm)" package="5 mm [THT]"]
  Composant1 = Arduino Uno (Rev3)
  R2 = Resistor [tolerance=±5% resistance=220 package=THT]
  LED2 = LED - 5mm [color="Red (633nm)" package="5 mm [THT]"]
  R3 = Resistor [tolerance=±5% resistance=220 package=THT]
  LED3 = LED - 5mm [color="Red (633nm)" package="5 mm [THT]"]
  R4 = Resistor [tolerance=±5% resistance=220 package=THT]
  LED4 = LED - 5mm [color="Red (633nm)" package="5 mm [THT]"]
  R5 = Resistor [tolerance=±5% resistance=220 package=THT]
  LED5 = LED - 5mm [color="Red (633nm)" package="5 mm [THT]"]
  R6 = Resistor [tolerance=±5% resistance=220 package=THT]
  LED6 = LED - 5mm [color="Red (633nm)" package="5 mm [THT]"]
  R7 = Resistor [tolerance=±5% resistance=220 package=THT]
  LED7 = LED - 5mm [color="Red (633nm)" package="5 mm [THT]"]
  R8 = Resistor [tolerance=±5% resistance=220 package=THT]
  LED8 = LED - 5mm [color="Red (633nm)" package="5 mm [THT]"]
  R9 = Resistor [tolerance=±5% resistance=220 package=THT]
  LED9 = LED - 5mm [color="Red (633nm)" package="5 mm [THT]"]
  R10 = Resistor [tolerance=±5% resistance=220 package=THT]
  LED10 = LED - 5mm [color="Red (633nm)" package="5 mm [THT]"]

nets:
  N1: R1.Pin_0, LED1.anode
  N2: R1.Pin_1, Composant1.D13/SCK
  N3: LED1.cathode, Composant1.GND, LED2.cathode, LED3.cathode, LED4.cathode, LED5.cathode, LED6.cathode, LED7.cathode, LED8.cathode, LED9.cathode, LED10.cathode
  N4: Composant1.D8, R6.Pin_1
  N5: Composant1.D9_PWM, R5.Pin_1
  N6: Composant1.D10_PWM/SS, R4.Pin_1
  N7: Composant1.D11_PWM/MOSI, R3.Pin_1
  N8: Composant1.D12/MISO, R2.Pin_1
  N9: Composant1.D4, R10.Pin_1
  N10: Composant1.D5_PWM, R9.Pin_1
  N11: Composant1.D6_PWM, R8.Pin_1
  N12: Composant1.D7, R7.Pin_1
  N13: R2.Pin_0, LED2.anode
  N14: R3.Pin_0, LED3.anode
  N15: R4.Pin_0, LED4.anode
  N16: R5.Pin_0, LED5.anode
  N17: R6.Pin_0, LED6.anode
  N18: R7.Pin_0, LED7.anode
  N19: R8.Pin_0, LED8.anode
  N20: R9.Pin_0, LED9.anode
  N21: R10.Pin_0, LED10.anode

// code stored in the sketch: Untitled.ino
#define sortie 13
#define freq 490
#define dutyCycle 2 // 100/dutycycle 10 pour 10%, 20 pour 5%
void setup() {
  // put your setup code here, to run once:
  pinMode(sortie, OUTPUT);
}
void loop() {
  // put your main code here, to run repeatedly:
  int period = 1000/freq;
  int timing = period / dutyCycle;
  digitalWrite(sortie, HIGH);
  delay(timing);
  digitalWrite(sortie, LOW);
  delay(period - timing);
}
